# Fritzing sketch schematic (saved by Fritzing 0.9.3b)
circuit board: 8.46667cm x 5.64444cm
breadboards: 1

parts:
  J1 = Basic Servo
  J2 = Basic Servo
  Part2 = Bluetooth HC-05 Macho
  IC1 = Voltage Regulator [package=to-220-alt]
  C2 = Electrolytic Capacitor [capacitance=1000µF package="300 mil [THT, electrolytic]"]
  VCC1 = Battery block 9V
  Part3 = Arduino Pro Mini (5V)
  VCC2 = Battery block 9V

nets:
  GND: J1.gnd, J2.gnd, Part2.GND, C2.-, VCC1.-, Part3.GND, VCC2.-
  VCC: J1.vcc, J2.vcc, IC1.OUT, C2.+
  N1: J1.pulse, Part3.D9
  N2: J2.pulse, Part3.D10
  N3: Part2.TXD, Part3.MISO
  N4: Part2.RXD, Part3.MOSI
  VCC_2: Part2.VCC, Part3.VCC
  N5: Part3.RAW, VCC2.+

// code stored in the sketch: test.ino
#include <SoftwareSerial.h>
#include <Servo.h>
SoftwareSerial BTserial(10, 11); // RX | TX
Servo ser1;
Servo ser2;
void setup() {
  Serial.begin(38400);
  BTserial.begin(9600); 
  ser1.attach(9);
  ser2.attach(8);
}

void loop() {

  String message = "";
  if(BTserial.available()>0){
    message = BTserial.read();
    Serial.println(message);
    char c[9];
    message.toCharArray(c, 9);
    int pos1 = 0, pos2 = 0;
    pos1 = strToInt(c, 0);
    for(int i = 0; c[i]!=';'; i++){
      if(c[i] == ','){
        pos2 = strToInt(c, i+1);
      }
    }
    ser1.write(pos1);
    ser2.write(pos2);
  }
  if(Serial.available()>0){
    BTserial.println(Serial.read());
  }
  delay(20);
}

int strToInt(char c[], int pos){
  char temp[3];
  for(int i = pos, k = 0; c[i]!=';' || c[i]!=','; i++){
    if(c[i]>'0' && c[i]<'9'){
      temp[k] = c[i];
      k++;
    }else return 0;
  }
  return atoi(c);
}
